// Logisim project unycicle.circ as structural Verilog: 5 circuits, main circuit main
module main (
);

  wire alu_1_zero, AluSrc, and_1_out, Branch, button_1_out, clock_1_out, clock_2_out, Jump, lui, MemRead,
       MemToReg, MemWrite, RegDst, RegWrite;
  wire [3:0] alu_control_1_op, AluOp;
  wire [4:0] multiplexer_1_out;
  wire [25:0] ram_1_dout;
  wire [27:0] bit_extender_1_out, shifter_1_out;
  wire [31:0] adder_1_out, adder_2_out, alu_1_result, bit_extender_2_out, multiplexer_2_out,
       multiplexer_3_out, multiplexer_4_out, multiplexer_5_out, multiplexer_6_out, ram_2_dout, register_1_q,
       registers_1_reada, registers_1_readb, shifter_2_out, shifter_3_out;
  wire [31:26] ram_1_dout_2;

  Clock clock_1 (.out(clock_1_out));
  Register #(.width(32)) register_1 (
    .D(multiplexer_2_out), .clk(clock_1_out), .Q(register_1_q), .clr(button_1_out));  // open: en
  Button button_1 (.out(button_1_out));
  Adder #(.width(32)) adder_1 (.a(32'h4), .b(register_1_q), .out(adder_1_out));  // open: cin, cout
  RAM #(.asyncread("true"), .dataWidth(32)) ram_1 (
    .addr(register_1_q[9:2]), .dout({ram_1_dout_2, ram_1_dout}));  // open: we, oe, clk, din
  assign bit_extender_1_out = {{2{ram_1_dout[25]}}, ram_1_dout};  // Bit_Extender bit_extender_1
  Shifter #(.width(28)) shifter_1 (.in(bit_extender_1_out), .\dist (5'b00010), .out(shifter_1_out));
  Multiplexer #(.width(5)) multiplexer_1 (
    .in0(ram_1_dout[20:16]), .in1(ram_1_dout[15:11]), .out(multiplexer_1_out), .sel(RegDst));
  assign bit_extender_2_out = {{16{ram_1_dout[15]}}, ram_1_dout[15:0]};  // Bit_Extender bit_extender_2
  Multiplexer #(.width(32)) multiplexer_2 (
    .in0(multiplexer_5_out), .in1({adder_1_out[31:28], shifter_1_out}), .out(multiplexer_2_out), .sel(Jump));
  Multiplexer #(.width(32)) multiplexer_3 (
    .in0(bit_extender_2_out), .in1(shifter_2_out), .out(multiplexer_3_out), .sel(lui));
  Shifter #(.width(32)) shifter_2 (.in(bit_extender_2_out), .\dist (5'b10000), .out(shifter_2_out));
  CONTROL control_1 (
    .opcode(ram_1_dout_2), .RegDst(RegDst), .Jump(Jump), .Branch(Branch), .MemRead(MemRead),
    .MemToReg(MemToReg), .AluOp(AluOp), .MemWrite(MemWrite), .AluSrc(AluSrc), .RegWrite(RegWrite), .lui(lui));
  REGISTERS registers_1 (
    .RegA(ram_1_dout[25:21]), .RegB(ram_1_dout[20:16]), .RegD(multiplexer_1_out), .Data(multiplexer_6_out),
    .RegWrite(RegWrite), .ReadA(registers_1_reada), .ReadB(registers_1_readb));
  Shifter #(.width(32)) shifter_3 (.in(multiplexer_3_out), .\dist (5'b00010), .out(shifter_3_out));
  Multiplexer #(.width(32)) multiplexer_4 (
    .in0(registers_1_readb), .in1(multiplexer_3_out), .out(multiplexer_4_out), .sel(AluSrc));
  ALU_CONTROL alu_control_1 (.funct(ram_1_dout[5:0]), .aluOp(AluOp), .op(alu_control_1_op));
  Adder #(.width(32)) adder_2 (.a(adder_1_out), .b(shifter_3_out), .out(adder_2_out));  // open: cin, cout
  Multiplexer #(.width(32)) multiplexer_5 (
    .in0(adder_1_out), .in1(adder_2_out), .out(multiplexer_5_out), .sel(and_1_out));
  and and_1 (and_1_out, Branch, alu_1_zero);
  ALU alu_1 (
    .OpA(registers_1_reada), .OpB(multiplexer_4_out), .OP(alu_control_1_op), .Zero(alu_1_zero),
    .Result(alu_1_result));
  RAM #(.addrWidth(24), .asyncread("true"), .dataWidth(32)) ram_2 (
    .addr(alu_1_result[23:0]), .we(MemWrite), .oe(MemRead), .clk(clock_2_out), .din(registers_1_readb),
    .dout(ram_2_dout));
  Clock clock_2 (.out(clock_2_out));
  Multiplexer #(.width(32)) multiplexer_6 (
    .in0(alu_1_result), .in1(ram_2_dout), .out(multiplexer_6_out), .sel(MemToReg));
endmodule

module REGISTERS (
  input  [4:0] RegA,
  input  [4:0] RegB,
  input  [4:0] RegD,
  input  [31:0] Data,
  input  RegWrite,
  output [31:0] ReadA,
  output [31:0] ReadB
);

  wire button_1_out, button_2_out, button_3_out, button_4_out, button_5_out, button_6_out, button_7_out,
       button_8_out, button_9_out, button_10_out, button_11_out, button_12_out, button_13_out, button_14_out,
       button_15_out, button_16_out, button_17_out, button_18_out, button_19_out, button_20_out,
       button_21_out, button_22_out, button_23_out, button_24_out, button_25_out, button_26_out,
       button_27_out, button_28_out, button_29_out, button_30_out, button_31_out, clk, en1, en2, en3, en4,
       en5, en6, en7, en8, en9, en10, en11, en12, en13, en14, en15, en16, en17, en18, en19, en20, en21, en22,
       en23, en24, en25, en26, en27, en28, en29, en30, en31;
  wire [31:0] rd0, rq1, rq2, rq3, rq4, rq5, rq6, rq7, rq8, rq9, rq10, rq11, rq12, rq13, rq14, rq15, rq16,
       rq17, rq18, rq19, rq20, rq21, rq22, rq23, rq24, rq25, rq26, rq27, rq28, rq29, rq30, rq31;

  Clock clock_1 (.out(clk));
  Multiplexer #(.select(5), .width(32)) multiplexer_1 (
    .in0(rd0), .in1(rq1), .in2(rq2), .in3(rq3), .in4(rq4), .in5(rq5), .in6(rq6), .in7(rq7), .in8(rq8),
    .in9(rq9), .in10(rq10), .in11(rq11), .in12(rq12), .in13(rq13), .in14(rq14), .in15(rq15), .in16(rq16),
    .in17(rq17), .in18(rq18), .in19(rq19), .in20(rq20), .in21(rq21), .in22(rq22), .in23(rq23), .in24(rq24),
    .in25(rq25), .in26(rq26), .in27(rq27), .in28(rq28), .in29(rq29), .in30(rq30), .in31(rq31), .out(ReadA),
    .sel(RegA));
  Multiplexer #(.select(5), .width(32)) multiplexer_2 (
    .in0(rd0), .in1(rq1), .in2(rq2), .in3(rq3), .in4(rq4), .in5(rq5), .in6(rq6), .in7(rq7), .in8(rq8),
    .in9(rq9), .in10(rq10), .in11(rq11), .in12(rq12), .in13(rq13), .in14(rq14), .in15(rq15), .in16(rq16),
    .in17(rq17), .in18(rq18), .in19(rq19), .in20(rq20), .in21(rq21), .in22(rq22), .in23(rq23), .in24(rq24),
    .in25(rq25), .in26(rq26), .in27(rq27), .in28(rq28), .in29(rq29), .in30(rq30), .in31(rq31), .out(ReadB),
    .sel(RegB));
  Decoder #(.select(5)) decoder_1 (
    .out1(en1), .out2(en2), .out3(en3), .out4(en4), .out5(en5), .out6(en6), .out7(en7), .out8(en8),
    .out9(en9), .out10(en10), .out11(en11), .out12(en12), .out13(en13), .out14(en14), .out15(en15),
    .out16(en16), .out17(en17), .out18(en18), .out19(en19), .out20(en20), .out21(en21), .out22(en22),
    .out23(en23), .out24(en24), .out25(en25), .out26(en26), .out27(en27), .out28(en28), .out29(en29),
    .out30(en30), .out31(en31), .sel(RegD), .en(RegWrite));  // open: out0
  Register #(.width(32)) r0 (.D(rd0), .Q(rd0), .clk(clk), .clr(1'b1));  // open: en
  Register #(.width(32)) r8 (.D(Data), .en(en8), .Q(rq8), .clk(clk), .clr(button_1_out));
  Button button_1 (.out(button_1_out));
  Register #(.width(32)) r16 (.D(Data), .en(en16), .Q(rq16), .clk(clk), .clr(button_2_out));
  Button button_2 (.out(button_2_out));
  Register #(.width(32)) r24 (.D(Data), .en(en24), .Q(rq24), .clk(clk), .clr(button_3_out));
  Button button_3 (.out(button_3_out));
  Register #(.width(32)) r1 (.D(Data), .en(en1), .Q(rq1), .clk(clk), .clr(button_4_out));
  Button button_4 (.out(button_4_out));
  Register #(.width(32)) r9 (.D(Data), .en(en9), .Q(rq9), .clk(clk), .clr(button_5_out));
  Button button_5 (.out(button_5_out));
  Register #(.width(32)) r17 (.D(Data), .en(en17), .Q(rq17), .clk(clk), .clr(button_6_out));
  Button button_6 (.out(button_6_out));
  Register #(.width(32)) r25 (.D(Data), .en(en25), .Q(rq25), .clk(clk), .clr(button_7_out));
  Button button_7 (.out(button_7_out));
  Register #(.width(32)) r2 (.D(Data), .en(en2), .Q(rq2), .clk(clk), .clr(button_8_out));
  Button button_8 (.out(button_8_out));
  Register #(.width(32)) r10 (.D(Data), .en(en10), .Q(rq10), .clk(clk), .clr(button_9_out));
  Button button_9 (.out(button_9_out));
  Register #(.width(32)) r18 (.D(Data), .en(en18), .Q(rq18), .clk(clk), .clr(button_10_out));
  Button button_10 (.out(button_10_out));
  Register #(.width(32)) r26 (.D(Data), .en(en26), .Q(rq26), .clk(clk), .clr(button_11_out));
  Button button_11 (.out(button_11_out));
  Register #(.width(32)) r3 (.D(Data), .en(en3), .Q(rq3), .clk(clk), .clr(button_12_out));
  Button button_12 (.out(button_12_out));
  Register #(.width(32)) r11 (.D(Data), .en(en11), .Q(rq11), .clk(clk), .clr(button_13_out));
  Button button_13 (.out(button_13_out));
  Register #(.width(32)) r19 (.D(Data), .en(en19), .Q(rq19), .clk(clk), .clr(button_14_out));
  Button button_14 (.out(button_14_out));
  Register #(.width(32)) r27 (.D(Data), .en(en27), .Q(rq27), .clk(clk), .clr(button_15_out));
  Button button_15 (.out(button_15_out));
  Register #(.width(32)) r4 (.D(Data), .en(en4), .Q(rq4), .clk(clk), .clr(button_16_out));
  Button button_16 (.out(button_16_out));
  Register #(.width(32)) r12 (.D(Data), .en(en12), .Q(rq12), .clk(clk), .clr(button_17_out));
  Button button_17 (.out(button_17_out));
  Register #(.width(32)) r20 (.D(Data), .en(en20), .Q(rq20), .clk(clk), .clr(button_18_out));
  Button button_18 (.out(button_18_out));
  Register #(.width(32)) r28 (.D(Data), .en(en28), .Q(rq28), .clk(clk), .clr(button_19_out));
  Button button_19 (.out(button_19_out));
  Register #(.width(32)) r5 (.D(Data), .en(en5), .Q(rq5), .clk(clk), .clr(button_20_out));
  Button button_20 (.out(button_20_out));
  Register #(.width(32)) r13 (.D(Data), .en(en13), .Q(rq13), .clk(clk), .clr(button_21_out));
  Button button_21 (.out(button_21_out));
  Register #(.width(32)) r21 (.D(Data), .en(en21), .Q(rq21), .clk(clk), .clr(button_22_out));
  Button button_22 (.out(button_22_out));
  Register #(.width(32)) r29 (.D(Data), .en(en29), .Q(rq29), .clk(clk), .clr(button_23_out));
  Button button_23 (.out(button_23_out));
  Register #(.width(32)) r6 (.D(Data), .en(en6), .Q(rq6), .clk(clk), .clr(button_24_out));
  Button button_24 (.out(button_24_out));
  Register #(.width(32)) r14 (.D(Data), .en(en14), .Q(rq14), .clk(clk), .clr(button_25_out));
  Button button_25 (.out(button_25_out));
  Register #(.width(32)) r22 (.D(Data), .en(en22), .Q(rq22), .clk(clk), .clr(button_26_out));
  Button button_26 (.out(button_26_out));
  Register #(.width(32)) r30 (.D(Data), .en(en30), .Q(rq30), .clk(clk), .clr(button_27_out));
  Button button_27 (.out(button_27_out));
  Register #(.width(32)) r7 (.D(Data), .en(en7), .Q(rq7), .clk(clk), .clr(button_28_out));
  Button button_28 (.out(button_28_out));
  Register #(.width(32)) r15 (.D(Data), .en(en15), .Q(rq15), .clk(clk), .clr(button_29_out));
  Button button_29 (.out(button_29_out));
  Register #(.width(32)) r23 (.D(Data), .en(en23), .Q(rq23), .clk(clk), .clr(button_30_out));
  Button button_30 (.out(button_30_out));
  Register #(.width(32)) r31 (.D(Data), .en(en31), .Q(rq31), .clk(clk), .clr(button_31_out));
  Button button_31 (.out(button_31_out));

  // Other names for the same wires on the sheet: en = RegWrite; read1[31:0] = ReadA; read2[31:0] = ReadB;
  //   rq0[31:0] = rd0; sel1[4:0] = RegA; sel2[4:0] = RegB; selwrite[4:0] = RegD; rd1[31:0] = Data; rd2[31:0] = Data;
  //   rd3[31:0] = Data; rd4[31:0] = Data; rd5[31:0] = Data; rd6[31:0] = Data; rd7[31:0] = Data; rd8[31:0] = Data;
  //   rd9[31:0] = Data; rd10[31:0] = Data; rd11[31:0] = Data; rd12[31:0] = Data; rd13[31:0] = Data; rd14[31:0] = Data;
  //   rd15[31:0] = Data; rd16[31:0] = Data; rd17[31:0] = Data; rd18[31:0] = Data; rd19[31:0] = Data;
  //   rd20[31:0] = Data; rd21[31:0] = Data; rd22[31:0] = Data; rd23[31:0] = Data; rd24[31:0] = Data;
  //   rd25[31:0] = Data; rd26[31:0] = Data; rd27[31:0] = Data; rd28[31:0] = Data; rd29[31:0] = Data;
  //   rd30[31:0] = Data; rd31[31:0] = Data; write[31:0] = Data
endmodule

module ALU (
  input  [31:0] OpA,
  input  [31:0] OpB,
  input  [3:0] OP,
  output Zero,
  output [31:0] Result
);

  wire [31:0] add_alu, and_alu, nor_alu, or_alu, slt_alu, sub_alu, xor_alu;

  assign and_alu = OpA & OpB;  // AND_Gate and_1, 32 bits wide
  assign or_alu = OpA | OpB;  // OR_Gate or_1, 32 bits wide
  assign nor_alu = ~(OpA | OpB);  // NOR_Gate nor_1, 32 bits wide
  Multiplexer #(.select(4), .width(32)) multiplexer_1 (
    .in0(and_alu), .in1(or_alu), .in2(add_alu), .in3(slt_alu), .in4(xor_alu), .in6(sub_alu), .in12(nor_alu),
    .out(Result), .sel(OP));  // open: in5, in7, in8, in9, in10, in11, in13, in14, in15
  Comparator #(.width(32)) comparator_1 (.a(OpA), .b(OpB), .eq(Zero));  // open: gt, lt
  Adder #(.width(32)) adder_1 (.a(OpA), .b(OpB), .out(add_alu));  // open: cin, cout
  Subtractor #(.width(32)) subtractor_1 (.a(OpA), .b(OpB), .out(sub_alu));  // open: bin, bout
endmodule

module CONTROL (
  input  [5:0] opcode,
  output RegDst,
  output Jump,
  output Branch,
  output MemRead,
  output MemToReg,
  output [3:0] AluOp,
  output MemWrite,
  output AluSrc,
  output RegWrite,
  output lui
);

  wire and_1_out, and_2_out, and_3_out, and_5_out, and_6_out, and_7_out, and_8_out, and_9_out, and_13_out,
       and_14_out, and_15_out, and_16_out, and_17_out, and_18_out, and_19_out, and_20_out, and_21_out,
       and_22_out, and_23_out, and_24_out, and_25_out, not_1_out, not_2_out, not_3_out, not_4_out, not_5_out,
       not_6_out;

  not not_1 (not_1_out, opcode[5]);
  not not_2 (not_2_out, opcode[4]);
  not not_3 (not_3_out, opcode[3]);
  not not_4 (not_4_out, opcode[2]);
  not not_5 (not_5_out, opcode[1]);
  not not_6 (not_6_out, opcode[0]);
  and and_1 (and_1_out, not_3_out, not_4_out, not_5_out);
  and and_2 (and_2_out, opcode[5], not_4_out, not_5_out);
  and and_3 (and_3_out, opcode[4], not_4_out, not_5_out);
  and and_4 (Jump, opcode[1], not_6_out);
  and and_5 (and_5_out, not_3_out, opcode[2]);
  and and_6 (and_6_out, opcode[2], not_5_out);
  and and_7 (and_7_out, opcode[2], not_6_out);
  and and_8 (and_8_out, opcode[4], opcode[2]);
  and and_9 (and_9_out, opcode[5], opcode[2]);
  and and_10 (MemRead, not_3_out, opcode[0]);
  and and_11 (MemToReg, not_3_out, opcode[0]);
  and and_12 (AluOp[1], not_1_out, not_2_out, opcode[3], not_4_out, opcode[1], not_6_out);
  and and_13 (and_13_out, opcode[5], not_2_out, not_4_out, opcode[1], opcode[0]);
  and and_14 (and_14_out, not_1_out, not_2_out, not_3_out, opcode[2], not_5_out, not_6_out);
  and and_15 (and_15_out, not_1_out, not_2_out, opcode[3], not_4_out, not_5_out);
  and and_16 (and_16_out, not_1_out, not_2_out, opcode[3], opcode[2], opcode[1], opcode[0]);
  and and_17 (and_17_out, opcode[3], not_4_out, opcode[1]);
  and and_18 (and_18_out, opcode[3], opcode[2], not_5_out);
  and and_19 (and_19_out, opcode[4], opcode[3]);
  and and_20 (and_20_out, opcode[5], opcode[3]);
  and and_21 (and_21_out, opcode[3], opcode[1], not_6_out);
  and and_22 (and_22_out, not_1_out, not_2_out, opcode[3], not_4_out, not_5_out);
  and and_23 (and_23_out, not_4_out, not_5_out);
  and and_24 (and_24_out, not_3_out, opcode[0]);
  and and_25 (and_25_out, not_1_out, not_2_out, opcode[2], opcode[1], opcode[0]);
  and and_26 (lui, not_1_out, not_2_out, opcode[3], opcode[2], opcode[1], opcode[0]);
  or or_1 (RegDst, and_1_out, and_2_out, and_3_out);
  or or_2 (Branch, and_5_out, and_6_out, and_7_out, and_8_out, and_9_out);
  or or_3 (AluOp[0], and_13_out, and_14_out, and_15_out, and_16_out);
  or or_4 (MemWrite, and_17_out, and_18_out, and_19_out, and_20_out, and_21_out);
  or or_5 (AluSrc, opcode[0], and_22_out);
  or or_6 (RegWrite, and_23_out, and_24_out, and_25_out);

  assign AluOp[3:2] = 2'b00;
endmodule

module ALU_CONTROL (
  input  [5:0] funct,
  input  [3:0] aluOp,
  output [3:0] op
);

  wire and_1_out, and_2_out, and_3_out, and_4_out, and_5_out, and_6_out, and_7_out, and_8_out, and_9_out,
       and_10_out, and_11_out, and_12_out, and_13_out, and_14_out, and_15_out, and_16_out, and_17_out,
       and_18_out, and_19_out, and_20_out, and_21_out, and_22_out, and_23_out, and_24_out, and_25_out,
       and_26_out, and_27_out, not_1_out, not_2_out, not_3_out, not_4_out, not_5_out, not_6_out, not_7_out,
       not_8_out, not_9_out;

  not not_1 (not_1_out, funct[5]);
  not not_2 (not_2_out, funct[4]);
  not not_3 (not_3_out, funct[3]);
  not not_4 (not_4_out, funct[2]);
  not not_5 (not_5_out, funct[1]);
  not not_6 (not_6_out, aluOp[3]);
  not not_7 (not_7_out, aluOp[2]);
  not not_8 (not_8_out, aluOp[1]);
  not not_9 (not_9_out, aluOp[0]);
  and and_1 (and_1_out, not_9_out, not_1_out, funct[1], funct[0]);
  and and_2 (and_2_out, aluOp[3], funct[1], funct[0]);
  and and_3 (and_3_out, not_9_out, funct[2], funct[1], funct[0]);
  and and_4 (and_4_out, not_9_out, funct[4], funct[1], funct[0]);
  and and_5 (and_5_out, aluOp[1], funct[1], funct[0]);
  and and_6 (and_6_out, aluOp[2], funct[1], funct[0]);
  and and_7 (and_7_out, not_9_out, not_1_out, funct[1]);
  and and_8 (and_8_out, not_9_out, not_3_out, funct[1]);
  and and_9 (and_9_out, not_9_out, funct[2], funct[1]);
  and and_10 (and_10_out, not_9_out, funct[4], funct[1]);
  and and_11 (and_11_out, aluOp[1], funct[1]);
  and and_12 (and_12_out, aluOp[2], funct[1]);
  and and_13 (and_13_out, aluOp[3], funct[1]);
  and and_14 (and_14_out, not_3_out, not_4_out);
  and and_15 (and_15_out, not_4_out, funct[1]);
  and and_16 (and_16_out, funct[2], not_6_out, not_7_out, not_8_out, aluOp[0]);
  and and_17 (and_17_out, funct[4], not_4_out);
  and and_18 (and_18_out, funct[5], not_4_out);
  and and_19 (and_19_out, not_1_out, not_5_out, funct[0], not_9_out);
  and and_20 (and_20_out, not_5_out, funct[0], aluOp[1]);
  and and_21 (and_21_out, not_5_out, funct[0], aluOp[2]);
  and and_22 (and_22_out, not_5_out, funct[0], aluOp[3]);
  and and_23 (and_23_out, funct[2], not_5_out, funct[0], not_9_out);
  and and_24 (and_24_out, not_1_out, not_2_out, funct[3], not_4_out, not_5_out);
  and and_25 (and_25_out, funct[5], not_2_out, funct[3], not_4_out, funct[1], not_6_out, not_7_out, not_8_out, not_9_out);
  and and_26 (and_26_out, funct[4], not_5_out, funct[0], not_9_out);
  and and_27 (and_27_out, funct[5], not_2_out, funct[3], not_4_out, funct[0], not_6_out, not_7_out, not_8_out, not_9_out);
  or or_1 (op[3], and_1_out, and_2_out, and_3_out, and_4_out, and_5_out, and_6_out);
  or or_2 (op[2], and_7_out, and_8_out, and_9_out, and_10_out, and_11_out, and_12_out, and_13_out);
  or or_3 (op[1], and_14_out, and_15_out, and_16_out, and_17_out, and_18_out);
  or or_4 (op[0], and_19_out, and_20_out, and_21_out, and_22_out, and_23_out, and_24_out, and_25_out, and_26_out, and_27_out);
endmodule
